# Fritzing sketch RPI_Shield (saved by Fritzing 0.9.2b)
breadboards: 1

parts:
  Motor_Driver = Motor Driver 1A Dual TB6612FNG
  Teensy_3_1 = Teensy 3.1
  Bluetooth_HC-05 = Header 4 [package=1x04-1mm-ra]
  Power_Supply = Header 2 [package=jst-2-pth-kit]
  5V_Output_RPI = Header 2 [package=jst-2-pth-kit]
  S1 = Toggle Switch [package=THT]
  2S_LiPo = DC Power [voltage=7.4]
  StepDown3_3V = Voltage Regulator - 3.3V [package="TO220 [THT]"]
  StepDown3_3V_2 = Voltage Regulator - 5V [package="DPak [SMD]"]
  C1 = Electrolytic Capacitor [capacitance=100µF package="100 mil [THT, electrolytic]"]
  C2 = Ceramic Capacitor [capacitance=100nF package="100 mil [THT, multilayer]"]
  C3 = Electrolytic Capacitor [capacitance=100µF package="100 mil [THT, electrolytic]"]
  C4 = Ceramic Capacitor [capacitance=100nF package="100 mil [THT, multilayer]"]
  Q1 = NPN-Transistor [package="SOT-23 [SMD]"]
  Buzzer = Piezo Speaker
  I2C_Bus_3_3V = Header 4 [package=1x04-1mm-ra]
  Neo_Pixel = Header 3 [package=jst-3-smd]
  R1 = Resistor [tolerance=±5% resistance=1k package=THT]
  Uart_RPI = Header 3 [package=jst-3-smd]
  NRF24 = Header 8 [package=1x08_smd_combined]
  Motor_B = Header 2 [package=jst-2-pth-kit]
  Motor_A = Header 2 [package=jst-2-pth-kit]

nets:
  GND: Motor_Driver.GND, Teensy_3_1.GND, Bluetooth_HC-05.4, 5V_Output_RPI.2, StepDown3_3V.GND, StepDown3_3V_2.GND, C1.-, C2.0, C3.-, C4.0, Q1.2, I2C_Bus_3_3V.4, Neo_Pixel.3, Uart_RPI.3, NRF24.8
  MOT_B1: Motor_Driver.B01, Motor_B.1
  MOT_B2: Motor_Driver.B02, Motor_B.2
  N1: Motor_Driver.A02, Motor_A.2
  N2: Motor_Driver.A01, Motor_A.1
  3.3V: Motor_Driver.VCC, Teensy_3_1.3V3, StepDown3_3V.output_voltage, C3.+, C4.1, Buzzer.pin1, I2C_Bus_3_3V.1, NRF24.1
  VIn: Motor_Driver.VM, S1.COM, StepDown3_3V.input_voltage, StepDown3_3V_2.input_voltage
  MOT_PWMA: Motor_Driver.PWMA, Teensy_3_1.A8/D22
  MOT_AIN2: Motor_Driver.AIN2, Teensy_3_1.A3/D17
  MOT_AIN1: Motor_Driver.AIN1, Teensy_3_1.A2/D16
  MOT_STBY: Motor_Driver.STBY, Teensy_3_1.A6/D20
  MOT_BIN1: Motor_Driver.BIN1, Teensy_3_1.A1/D15
  MOT_BIN2: Motor_Driver.BIN2, Teensy_3_1.A0/D14
  MOT_PWMB: Motor_Driver.PWMB, Teensy_3_1.A7/D21
  PI_Rx: Teensy_3_1.D0, Uart_RPI.1
  PI_Tx: Teensy_3_1.D1, Uart_RPI.2
  NRF_CSN: Teensy_3_1.D2, NRF24.3
  NRF_IRQ: Teensy_3_1.D5, NRF24.7
  NRF_CE: Teensy_3_1.D6, NRF24.2
  BTM_Rx: Teensy_3_1.D9, Bluetooth_HC-05.2
  BTM_Tx: Teensy_3_1.D10, Bluetooth_HC-05.3
  NRF_MOSI: Teensy_3_1.D11, NRF24.5
  NRF_MISO: Teensy_3_1.D12, NRF24.6
  NRF_SCK: Teensy_3_1.D13, NRF24.4
  I2C_SDA: Teensy_3_1.A4/D18, I2C_Bus_3_3V.2
  I2C_SCL: Teensy_3_1.A5/D19, I2C_Bus_3_3V.3
  NEO_Pin: Teensy_3_1.A9/D23, Neo_Pixel.2
  5V: Bluetooth_HC-05.1, 5V_Output_RPI.1, StepDown3_3V_2.output_voltage, C1.+, C2.1, Neo_Pixel.1
  N3: Power_Supply.1, S1.L1, 2S_LiPo.V+
  N4: Power_Supply.2, 2S_LiPo.V-
  N5: Q1.0, R1.Pin_1
  N6: Q1.1, Buzzer.pin2
  Buzz_Pin: R1.Pin_0

notes:
  Prototype RPI_Shield, V .01
